// Logisim project Project2KritinRane.circ as structural Verilog: 1 circuit, main circuit main
module main (
);

  wire and_1_out, and_2_out, and_3_out, and_4_out, and_5_out, and_6_out, and_7_out, clock_1_out,
       decoder_1_out0, decoder_1_out1, decoder_1_out2, decoder_1_out3, not_1_out, not_2_out;
  wire [7:0] adder_1_out, adder_2_out, memData_dout, multiplexer_1_out, multiplexer_2_out, multiplexer_3_out,
       multiplexer_4_out, multiplexer_5_out, multiplexer_6_out, PC_q, subtractor_1_out, X0_q, X1_q, X2_q,
       X3_q;
  wire [15:0] instruct_mem_dout;

  Clock clock_1 (.out(clock_1_out));
  RAM #(.dataWidth(16), .enables("line")) instruct_mem (
    .addr(PC_q), .we(1'b0), .clk(clock_1_out), .dout(instruct_mem_dout));  // open: din
  Hex_Digit_Display hex_digit_display_1 (.value(PC_q[7:4]));  // open: dp
  Hex_Digit_Display hex_digit_display_2 (.value(PC_q[3:0]));  // open: dp
  Adder adder_1 (.a(PC_q), .b(8'h1), .out(adder_1_out));  // open: cin, cout
  Register PC (.D(adder_1_out), .en(1'b1), .clk(clock_1_out), .Q(PC_q));  // open: clr
  Decoder #(.select(2)) decoder_1 (
    .out0(decoder_1_out0), .out1(decoder_1_out1), .out2(decoder_1_out2), .out3(decoder_1_out3),
    .sel(instruct_mem_dout[1:0]));  // open: en
  and and_1 (and_1_out, instruct_mem_dout[14], instruct_mem_dout[15]);
  not not_1 (not_1_out, and_1_out);
  Register X0 (.D(multiplexer_6_out), .en(and_2_out), .clk(clock_1_out), .Q(X0_q));  // open: clr
  and and_2 (and_2_out, decoder_1_out0, not_1_out);
  Register X1 (.D(multiplexer_6_out), .en(and_3_out), .clk(clock_1_out), .Q(X1_q));  // open: clr
  and and_3 (and_3_out, decoder_1_out1, not_1_out);
  Register X2 (.D(multiplexer_6_out), .en(and_4_out), .clk(clock_1_out), .Q(X2_q));  // open: clr
  and and_4 (and_4_out, decoder_1_out2, not_1_out);
  Register X3 (.D(multiplexer_6_out), .en(and_5_out), .clk(clock_1_out), .Q(X3_q));  // open: clr
  and and_5 (and_5_out, decoder_1_out3, not_1_out);
  Multiplexer #(.select(2), .width(8)) multiplexer_1 (
    .in0(X0_q), .in1(X1_q), .in2(X2_q), .in3(X3_q), .out(multiplexer_1_out), .sel(instruct_mem_dout[3:2]));
  Multiplexer #(.select(2), .width(8)) multiplexer_2 (
    .in0(X0_q), .in1(X1_q), .in2(X2_q), .in3(X3_q), .out(multiplexer_2_out), .sel(instruct_mem_dout[12:11]));
  Adder adder_2 (.a(multiplexer_1_out), .b(multiplexer_3_out), .out(adder_2_out));  // open: cin, cout
  Multiplexer #(.width(8)) multiplexer_3 (
    .in0(instruct_mem_dout[11:4]), .in1(multiplexer_2_out), .out(multiplexer_3_out),
    .sel(instruct_mem_dout[13]));
  Multiplexer #(.select(2), .width(8)) multiplexer_4 (
    .in0(X0_q), .in1(X1_q), .in2(X2_q), .in3(X3_q), .out(multiplexer_4_out), .sel(instruct_mem_dout[1:0]));
  Subtractor subtractor_1 (.a(multiplexer_1_out), .b(multiplexer_3_out), .out(subtractor_1_out));  // open: bin, bout
  and and_6 (and_6_out, instruct_mem_dout[15], instruct_mem_dout[14]);
  not not_2 (not_2_out, and_6_out);
  Multiplexer #(.width(8)) multiplexer_5 (
    .in0(adder_2_out), .in1(subtractor_1_out), .out(multiplexer_5_out), .sel(and_7_out));
  and and_7 (and_7_out, not_2_out, instruct_mem_dout[14]);
  Multiplexer #(.width(8)) multiplexer_6 (
    .in0(multiplexer_5_out), .in1(memData_dout), .out(multiplexer_6_out), .sel(instruct_mem_dout[15]));
  Hex_Digit_Display hex_digit_display_3 (.value(multiplexer_1_out[7:4]));  // open: dp
  Hex_Digit_Display hex_digit_display_4 (.value(multiplexer_3_out[7:4]));  // open: dp
  Hex_Digit_Display hex_digit_display_5 (.value(multiplexer_1_out[3:0]));  // open: dp
  Hex_Digit_Display hex_digit_display_6 (.value(multiplexer_3_out[3:0]));  // open: dp
  RAM #(.enables("line")) memData (
    .addr(multiplexer_5_out), .we(and_1_out), .clk(clock_1_out), .din(multiplexer_4_out), .dout(memData_dout));

  // Notes on the sheet:
  //   I pledge my honor that I have abided by the Stevens Honor System. 
  //   Kritin Rane 
  //   program counter
  //   QuacksCPU
  //   Reg2
  //   Reg1
endmodule
